# Fritzing sketch arduinoDomoticaSchematic (saved by Fritzing 0.8.7b)
breadboards: 1

parts:
  R1 = Rotary Potentiometer (Small) [maximum_resistance=100kΩ package=THT]
  LED3 = smd LED [color="Orange (620nm)" part_number=corredor package="0603 [SMD]"]
  LED4 = smd LED [color="Blue (505nm)" part_number=copa package="0603 [SMD]"]
  LED5 = smd LED [color="Yellow (592nm)" part_number=cozinha package="0603 [SMD]"]
  LED6 = smd LED [color="Green (555nm)" part_number=sala package="0603 [SMD]"]
  R2 = Resistor [package="2010 [SMD]"]
  R6 = Rotary Potentiometer (Small) [maximum_resistance=100kΩ package=THT]
  S1 = H-Bridge with L298N
  M2 = DC Motor  # not connected
  Componente1 = Arduino Uno (Rev3)
  R7 = Resistor [package="2010 [SMD]"]
  R8 = Resistor [package="2010 [SMD]"]
  R9 = Resistor [package="2010 [SMD]"]
  U1 = RELAY [package=relay-jzc]
  U2 = RELAY [package=relay-jzc]
  IR1 = TSOP312.., 314.. [package=THT]
  R10 = Resistor [package="2010 [SMD]"]
  D1 = LTE-302 [part_number="Tv/ Home" package=lte-302]
  S2 = Pushbutton [package="[THT]"]
  S3 = Pushbutton [package="[THT]"]
  R11 = Resistor [package="2010 [SMD]"]
  R12 = Resistor [package="2010 [SMD]"]
  M3 = DC Motor  # not connected

nets:
  5V: R1.leg1, R6.leg1, S1.5V, Componente1.5V, IR1.Vs
  N1: R1.wiper, Componente1.A5/SCL
  GND: R1.leg2, R6.leg2, S1.GND, Componente1.GND, IR1.Data, R10.Pin_1, R11.Pin_1, R12.Pin_1
  N2: LED3.cathode, LED5.cathode, U1.NO, U1.COIL1, U2.NO, U2.COIL1
  N3: LED3.anode, R7.Pin_1
  N4: LED4.cathode, Componente1.D10_PWM/SS
  N5: LED4.anode, R8.Pin_1
  N6: LED5.anode, R2.Pin_1
  N7: LED6.cathode, Componente1.D9_PWM
  N8: LED6.anode, R9.Pin_1
  N9: R2.Pin_0, R7.Pin_0, R8.Pin_0, R9.Pin_0, U1.COIL2, U2.COIL2
  N10: R6.wiper, Componente1.A4/SDA
  N11: S1.IN3, Componente1.D6_PWM
  N12: S1.IN4, Componente1.D5_PWM
  N13: Componente1.A0, S3.Pin_1, S3.Pin_2, R12.Pin_0
  N14: Componente1.A1, S2.Pin_1, S2.Pin_2, R11.Pin_0
  N15: Componente1.D8, U1.NC
  N16: Componente1.D11_PWM/MOSI, IR1.GND
  N17: Componente1.D3_PWM, D1.A
  N18: Componente1.D7, U2.NC
  N19: U1.MAIN, U2.MAIN
  N20: R10.Pin_0, D1.C
  N21: S2.Pin_3, S2.Pin_4
  N22: S3.Pin_3, S3.Pin_4

notes:
  Controle das Persianas
  Cena 1 - Entretenimento
  Sala
  Copa
  Cozinha
  Corredor
  Cena 2 -
  Jantar
  Sistema de Iluminação
  Áudio e Vídeo

custom parts:
  H-Bridge with L298N: h-bridge
